# Fritzing sketch WiringDiagram (saved by Fritzing 0.9.3b)
breadboards: 1

parts:
  Part1 = Arduino Uno (Rev3)
  X1 = X113647 Stepper Driver Board [package=board]
  X2 = X113647 Stepper Driver Board [package=board]
  X4 = X113647 Stepper Driver Board [package=board]
  X3 = X113647 Stepper Driver Board [package=board]

nets:
  N1: Part1.A0, X1.IN1, X4.IN4
  N2: Part1.A1, X1.IN2, X4.IN3
  N3: Part1.A2, X1.IN3, X4.IN2
  N4: Part1.A3, X1.IN4, X4.IN1
  N5: Part1.D8, X2.IN4
  N6: Part1.D9_PWM, X2.IN3
  N7: Part1.D12/MISO, X2.IN2
  N8: Part1.D13/SCK, X2.IN1
  N9: Part1.D2, X3.IN4
  N10: Part1.D3_PWM, X3.IN3
  N11: Part1.D4, X3.IN2
  N12: Part1.D5_PWM, X3.IN1
  GND: X1.GND, X2.GND, X4.GND, X3.GND
  N13: X1.+V, X2.+V, X4.+V, X3.+V

notes:
  Note the Connection Circles between.
  Y-Left
  Y-Right
  X-Axis
  Z-Axis

custom parts:
  X113647 Stepper Driver Board: A common stepper motor driver board based on ULN2003APG darlington array
